# Fritzing sketch CG_Scale_v4.1 (saved by Fritzing 0.9.4)
circuit board: 4.1cm x 5.1cm
breadboards: 1

parts:
  -_+ = Battery block 9V
  R1 = Resistor [tolerance=±5% resistance=10k package=THT]
  R2 = Resistor [tolerance=±5% resistance=4.7k package=THT]
  keypad = female pin header, 3 pins [form="♀ (female)"]
  OLED = female pin header, 4 pins [form="♀ (female)"]
  Arduino_pro_mini_5v = Arduino Pro Mini (5V)
  Avant_/_Front = HX711 Weighing Sensor Module
  Arrière_/_Back = HX711 Weighing Sensor Module

nets:
  GND: -_+.-, keypad.pin3, OLED.pin4, Avant_/_Front.GND, Arrière_/_Back.GND
  N1: -_+.+, R1.Pin_1, Arduino_pro_mini_5v.RAW
  N2: R1.Pin_0, R2.Pin_1, Arduino_pro_mini_5v.A7
  N3: R2.Pin_0, Arduino_pro_mini_5v.GND
  N4: keypad.pin1, Arduino_pro_mini_5v.A6
  VCC: keypad.pin2, OLED.pin3, Arduino_pro_mini_5v.VCC, Avant_/_Front.VCC, Arrière_/_Back.VCC
  N5: OLED.pin1, Arduino_pro_mini_5v.A5
  N6: OLED.pin2, Arduino_pro_mini_5v.A4
  N7: Arduino_pro_mini_5v.A3, Avant_/_Front.CK/TX
  N8: Arduino_pro_mini_5v.A2, Avant_/_Front.DO/RX
  N9: Arduino_pro_mini_5v.A1, Arrière_/_Back.CK/TX
  N10: Arduino_pro_mini_5v.A0, Arrière_/_Back.DO/RX

notes:
  GND
  CK/TX
  DO/RX
  VCC
  OUT
  SDA
  SCL
  CG Scale - v3.1
  vert
  noir
  N
  blanc
  rouge

custom parts:
  HX711 Weighing Sensor Module: HX711 is a precision 24-bit analog-to-digital converter (ADC) designed for weigh scales and industrial control applications to interface directly with a bridge sensor.
